# Fritzing sketch schematic (saved by Fritzing 0.7.11b)
stripboards: 1

parts:
  R1 = Resistor [tolerance=±5% resistance=10k package=THT]
  R2 = Resistor [tolerance=±5% resistance=10k package=THT]
  R3 = Resistor [tolerance=±5% resistance=10k package=THT]
  R4 = Resistor [tolerance=±5% resistance=10k package=THT]
  S1 = Pushbutton [package="[THT]"]
  S2 = Pushbutton [package="[THT]"]
  S3 = Pushbutton [package="[THT]"]
  S4 = Pushbutton [package="[THT]"]
  RPi_GPIO2 = RPi GPIO Header [form="♂ (shrouded male)" package=THT]
  J3 = ST7735 TFT LCD [form="♂ (male)" package=THT]

nets:
  +3.3V: R1.Pin_0, R2.Pin_0, R3.Pin_0, R4.Pin_0, RPi_GPIO2.+3.3V, J3.VCC, J3.LED+
  N1: R1.Pin_1, S1.Pin_3, S1.Pin_4, RPi_GPIO2.GPIO_22
  N2: R2.Pin_1, S2.Pin_1, S2.Pin_2, RPi_GPIO2.GPIO_25
  N3: R3.Pin_1, S3.Pin_1, S3.Pin_2, RPi_GPIO2.GPIO_17
  N4: R4.Pin_1, S4.Pin_1, S4.Pin_2, RPi_GPIO2.GPIO_14_(UART_TxD), J3.NC#2
  N5: S1.Pin_1, S1.Pin_2, S2.Pin_3, S2.Pin_4, S3.Pin_3, S3.Pin_4, S4.Pin_3, S4.Pin_4, RPi_GPIO2.Ground, J3.GND, J3.LED-
  N6: RPi_GPIO2.GPIO_10_(SPI_MOSI), J3.SDA
  N7: RPi_GPIO2.GPIO_11_(SPI_SCLK), J3.SCK
  N8: RPi_GPIO2.GPIO_7_(SPI_CS1), J3.SD-CS
  N9: RPi_GPIO2.GPIO_8_(SPI_CS0), J3.CS
  N10: RPi_GPIO2.GPIO_24, J3.RESET
  N11: RPi_GPIO2.GPIO_23, J3.A0

notes:
  RPi / PCD8544 header
  (c) Richard Hull 2013

custom parts:
  ST7735 TFT LCD: Generic single row male header
